// Logisim project Corcuitos lógicos - 2° período.circ as structural Verilog: 3 circuits, main circuit main
module main (
  input  B3,
  input  B2,
  input  B1,
  input  B0,
  input  ADD_SUB,
  output Cout,
  output Overflow,
  output S3,
  output S2,
  output S1,
  output S0
);

  wire Clear_out, d_ff_1_q, d_ff_3_q, d_ff_6_q, d_ff_7_q, Load_out, overflow_1_ovr, somador_1_s,
       somador_2_cout, somador_2_s, somador_3_cout, somador_3_s, somador_4_cout, somador_4_s, Transfer_out,
       X0_out, X1_out, X2_out, X3_out;

  Button Load (.out(Load_out));
  Button Transfer (.out(Transfer_out));
  Button Clear (.out(Clear_out));
  Overflow overflow_1 (.A3(S3), .X3(X3_out), .S3(somador_1_s), .OVR(overflow_1_ovr));
  D_Flip_Flop d_ff_1 (.clk(Load_out), .D(B3), .Q(d_ff_1_q));  // open: Qn, preset, en, reset
  xor X3 (X3_out, ADD_SUB, d_ff_1_q);
  Somador somador_1 (.A(S3), .X(X3_out), .Cin(somador_2_cout), .S(somador_1_s), .Cout(Cout));
  D_Flip_Flop d_ff_2 (.clk(Transfer_out), .D(overflow_1_ovr), .Q(Overflow));  // open: Qn, preset, en, reset
  D_Flip_Flop d_ff_3 (.clk(Load_out), .D(B2), .Q(d_ff_3_q));  // open: Qn, preset, en, reset
  xor X2 (X2_out, ADD_SUB, d_ff_3_q);
  D_Flip_Flop d_ff_4 (.clk(Transfer_out), .D(somador_1_s), .Q(S3), .reset(Clear_out));  // open: Qn, preset, en
  Somador somador_2 (.A(S2), .X(X2_out), .Cin(somador_3_cout), .S(somador_2_s), .Cout(somador_2_cout));
  D_Flip_Flop d_ff_5 (.clk(Transfer_out), .D(somador_2_s), .Q(S2), .reset(Clear_out));  // open: Qn, preset, en
  D_Flip_Flop d_ff_6 (.clk(Load_out), .D(B1), .Q(d_ff_6_q));  // open: Qn, preset, en, reset
  xor X1 (X1_out, ADD_SUB, d_ff_6_q);
  Somador somador_3 (.A(S1), .X(X1_out), .Cin(somador_4_cout), .S(somador_3_s), .Cout(somador_3_cout));
  D_Flip_Flop d_ff_7 (.clk(Load_out), .D(B0), .Q(d_ff_7_q));  // open: Qn, preset, en, reset
  xor X0 (X0_out, ADD_SUB, d_ff_7_q);
  Somador somador_4 (.A(S0), .X(X0_out), .Cin(ADD_SUB), .S(somador_4_s), .Cout(somador_4_cout));
  D_Flip_Flop d_ff_8 (.clk(Transfer_out), .D(somador_3_s), .Q(S1), .reset(Clear_out));  // open: Qn, preset, en
  D_Flip_Flop d_ff_9 (.clk(Transfer_out), .D(somador_4_s), .Q(S0), .reset(Clear_out));  // open: Qn, preset, en
endmodule

module Somador (
  input  A,
  input  X,
  input  Cin,
  output S,
  output Cout
);

  wire and_1_out, and_2_out, and_3_out, xor_1_out;

  xor xor_1 (xor_1_out, X, Cin);
  and and_1 (and_1_out, Cin, X);
  and and_2 (and_2_out, Cin, A);
  and and_3 (and_3_out, X, A);
  xor xor_2 (S, A, xor_1_out);
  or or_1 (Cout, and_1_out, and_2_out, and_3_out);
endmodule

module Overflow (
  input  A3,
  input  X3,
  input  S3,
  output OVR
);

  wire and_1_out, and_2_out;

  and and_1 (and_1_out, ~S3, X3, A3);  // AND_Gate
  and and_2 (and_2_out, S3, ~X3, ~A3);  // AND_Gate
  or or_1 (OVR, and_1_out, and_2_out);
endmodule
